// Logisim project MineSweeper.circ as structural Verilog: 6 circuits, main circuit main
module main (
);

  wire and_2_out, and_3_out, and_5_out, and_6_out, and_7_out, and_8_out, and_9_out, and_10_out, and_11_out,
       and_12_out, and_13_out, and_14_out, and_15_out, and_21_out, and_24_out, and_25_out, and_26_out,
       and_27_out, and_28_out, and_29_out, and_30_out, and_32_out, and_33_out, and_34_out, and_35_out,
       and_36_out, and_37_out, and_38_out, and_40_out, and_44_out, and_45_out, and_46_out, and_47_out,
       and_48_out, and_49_out, and_51_out, and_52_out, and_53_out, Btn_Flag, Btn_Uncover, CLK, clock_1_out,
       CLS, comparator_1_eq, comparator_2_eq, comparator_2_gt, comparator_2_lt, comparator_3_eq,
       comparator_3_gt, comparator_3_lt, comparator_4_eq, comparator_5_lt, comparator_6_eq, comparator_8_eq,
       comparator_8_gt, comparator_8_lt, comparator_9_eq, comparator_10_eq, comparator_11_eq,
       comparator_11_gt, comparator_11_lt, comparator_12_eq, comparator_13_eq, comparator_14_eq,
       comparator_15_eq, comparator_16_eq, comparator_17_eq, comparator_18_eq, comparator_19_eq,
       comparator_20_eq, comparator_21_eq, comparator_22_eq, comparator_23_gt, comparator_24_eq,
       comparator_25_gt, comparator_26_lt, comparator_27_gt, comparator_27_lt, comparator_28_gt,
       comparator_28_lt, comparator_29_eq, comparator_29_gt, comparator_31_eq, comparator_32_eq,
       comparator_32_lt, comparator_33_eq, comparator_33_gt, comparator_33_lt, comparator_34_eq,
       comparator_35_eq, comparator_36_eq, comparator_37_eq, comparator_38_eq, comparator_39_eq,
       comparator_40_eq, comparator_41_eq, d_ff_13_q, j_k_ff_1_q, nor_1_out, not_2_out, not_3_out, not_4_out,
       not_5_out, OP2_FINISH, OP3_FINISH, OP4_FINISH, OP5_FINISH, OP6_FINISH, OP7_FINISH, OP8_FINISH,
       OP9_FINISH, OPA_FINISH, or_1_out, or_2_out, or_3_out, or_4_out, or_5_out, or_6_out, or_7_out,
       or_8_out, or_9_out, or_10_out, or_13_out, or_14_out, or_15_out, or_16_out, or_17_out, or_19_out,
       or_20_out, or_21_out, or_22_out, or_26_out, or_29_out, or_gate_16bit_1_q, or_gate_16bit_2_q,
       rgb_video_1_p1, s_r_ff_1_q, s_r_ff_2_q, Start_Game_out, t_ff_1_q, t_ff_2_q, t_ff_3_q;
  wire [1:0] counter_10_q;
  wire [2:0] counter_5_q, counter_8_q, multiplexer_2_out, SquareWithFlag_data, UncoveredEmptySquare_data,
       UncoveredEmptySquareWith1_data, UncoveredEmptySquareWith2_data, UncoveredEmptySquareWith3_data,
       UncoveredEmptySquareWith4_data, UncoveredEmptySquareWith5_data, UncoveredEmptySquareWith6_data,
       UncoveredEmptySquareWith7_data, UncoveredEmptySquareWith8_data, UncoveredMineSquare_data;
  wire [3:0] adder_13_out, bit_extender_7_out, bit_extender_18_out, bitselector_1_out, bitselector_2_out,
       controlled_buffer_18_out, controlled_buffer_19_out, controlled_buffer_20_out,
       controlled_buffer_21_out, counter_2_q, counter_4_q, counter_12_q, encoder_4bit_1_o, encoder_4bit_2_o,
       OP6_Column, OP6_Row, OPCODE, or_27_out, RAM_OUTPUT, rom_1_data;
  wire [4:0] adder_9_out, counter_6_q, counter_11_q, divider_1_out;
  wire [5:0] adder_1_out, bit_extender_1_out, bit_extender_4_out, counter_9_q, multiplier_2_out;
  wire [6:0] adder_2_out, adder_3_out, adder_5_out, adder_6_out, and_17_out, and_18_out, and_19_out,
       and_20_out, bit_extender_2_out, bit_extender_3_out, bit_extender_5_out, bit_extender_6_out,
       bit_extender_10_out, bit_extender_12_out, counter_1_q, multiplier_1_out, multiplier_3_out,
       multiplier_4_out, multiplier_6_out, not_1_out, or_11_out, or_12_out;
  wire [7:0] adder_4_out, adder_7_out, adder_8_out, adder_10_out, adder_11_out, adder_12_out, ADDR,
       and_41_out, and_42_out, and_43_out, bit_extender_8_out, bit_extender_9_out, bit_extender_11_out,
       bit_extender_13_out, bit_extender_14_out, bit_extender_15_out, bit_extender_16_out,
       bit_extender_17_out, controlled_buffer_8_out, controlled_buffer_9_out, controlled_buffer_10_out,
       controlled_buffer_11_out, controlled_buffer_14_out, controlled_buffer_15_out,
       controlled_buffer_16_out, controlled_buffer_17_out, counter_13_q, JUMP_ADDR, multiplexer_5_out,
       multiplier_5_out, multiplier_7_out, OP6_JUMP_ADDR, or_18_out, pull_resistor_3_node,
       pull_resistor_4_node, pull_resistor_5_node, pull_resistor_6_node, pull_resistor_7_node, RAM_ADDR,
       random_1_out, register_1_q, register_3_q, subtractor_1_out, subtractor_2_out, subtractor_3_out,
       subtractor_4_out;
  wire [8:0] counter_7_q;
  wire [14:0] multiplexer_3_out;
  wire [15:0] Btn_Column, Btn_Row, controlled_buffer_1_out, controlled_buffer_2_out, controlled_buffer_3_out,
       controlled_buffer_4_out, decoder_4bit_1_o, decoder_4bit_2_o;
  wire [16:0] controlled_buffer_22_out, controlled_buffer_23_out, multiplexer_4_out, OP3_RAM, OP4_RAM,
       OP6_RAM, OP7_RAM, OP8_RAM, OP9_RAM, OPA_RAM, ram_encoder_5_encode, ram_encoder_6_encode;
  wire [28:0] OP2_CANVAS, OP7_CANVAS, rgb_video_1_p4;

  Comparator #(.width(4)) comparator_1 (.a(4'b0001), .b(OPCODE), .eq(comparator_1_eq));  // open: gt, lt
  Comparator #(.width(4)) comparator_2 (
    .a(4'b0010), .b(OPCODE), .gt(comparator_2_gt), .eq(comparator_2_eq), .lt(comparator_2_lt));
  Comparator #(.width(4)) comparator_3 (
    .a(4'b0111), .b(OPCODE), .gt(comparator_3_gt), .eq(comparator_3_eq), .lt(comparator_3_lt));
  or or_1 (or_1_out, or_8_out, or_6_out);
  ROM #(.addrWidth(6), .dataWidth(3)) UncoveredMineSquare (.addr(adder_1_out), .data(UncoveredMineSquare_data));
  ROM #(.addrWidth(6), .dataWidth(3)) SquareWithFlag (.addr(adder_1_out), .data(SquareWithFlag_data));
  ROM #(.addrWidth(6), .dataWidth(3)) UncoveredEmptySquare (.addr(adder_1_out), .data(UncoveredEmptySquare_data));
  ROM #(.addrWidth(6), .dataWidth(3)) UncoveredEmptySquareWith1 (
    .addr(adder_1_out), .data(UncoveredEmptySquareWith1_data));
  ROM #(.addrWidth(6), .dataWidth(3)) UncoveredEmptySquareWith2 (
    .addr(adder_1_out), .data(UncoveredEmptySquareWith2_data));
  ROM #(.addrWidth(6), .dataWidth(3)) UncoveredEmptySquareWith3 (
    .addr(adder_1_out), .data(UncoveredEmptySquareWith3_data));
  S_R_Flip_Flop #(.trigger("falling")) s_r_ff_1 (
    .S(1'b1), .R(1'b0), .clk(and_3_out), .Q(s_r_ff_1_q), .reset(or_1_out));  // open: Qn, preset
  or or_2 (or_2_out, CLS, OP2_FINISH, OP3_FINISH, OP4_FINISH);
  or or_3 (or_3_out, OP5_FINISH, OP6_FINISH, OP7_FINISH, OP8_FINISH);
  or or_4 (or_4_out, OP9_FINISH, OPA_FINISH, 1'b0, 1'b0);
  and and_1 (CLS, ~Start_Game_out, comparator_1_eq, CLK);  // AND_Gate
  or or_5 (or_5_out, comparator_2_gt, comparator_2_lt);
  and and_2 (and_2_out, comparator_2_eq, CLK);
  or or_6 (or_6_out, comparator_3_gt, comparator_3_lt);
  and and_3 (and_3_out, comparator_3_eq, CLK);
  S_R_Flip_Flop #(.trigger("falling")) s_r_ff_2 (
    .S(s_r_ff_1_q), .R(1'b0), .clk(and_3_out), .Q(s_r_ff_2_q), .reset(or_1_out));  // open: Qn, preset
  assign controlled_buffer_1_out = comparator_4_eq ? decoder_4bit_1_o : 16'bz;  // Controlled_Buffer controlled_buffer_1
  Decoder_4bit decoder_4bit_1 (.I(OP6_Column), .O(decoder_4bit_1_o));
  assign controlled_buffer_2_out = comparator_4_eq ? decoder_4bit_2_o : 16'bz;  // Controlled_Buffer controlled_buffer_2
  Decoder_4bit decoder_4bit_2 (.I(OP6_Row), .O(decoder_4bit_2_o));
  Comparator #(.mode("unsigned"), .width(4)) comparator_4 (
    .a(OPCODE), .b(4'b0110), .eq(comparator_4_eq));  // open: gt, lt
  Clock clock_1 (.out(clock_1_out));
  or or_7 (or_7_out, or_2_out, or_3_out, or_4_out);
  Counter #(.max('h1f), .trigger("falling"), .width(7)) counter_1 (
    .clr(or_5_out), .clk(and_2_out), .Q(counter_1_q));  // open: load, up, count, D, carry
  Counter #(.max('hf), .trigger("falling"), .width(4)) counter_2 (
    .clr(or_5_out), .clk(and_9_out), .Q(counter_2_q));  // open: load, up, count, D, carry
  Comparator #(.mode("unsigned"), .width(4)) comparator_5 (
    .a(4'b0001), .b(RAM_OUTPUT), .lt(comparator_5_lt));  // open: gt, eq
  Pull_Resistor pull_resistor_1 (.node(controlled_buffer_2_out));
  Button Start_Game (.out(Start_Game_out));
  and and_4 (CLK, ~Start_Game_out, clock_1_out);  // AND_Gate
  Comparator #(.width(4)) comparator_6 (.a(rom_1_data), .b(4'b0101), .eq(comparator_6_eq));  // open: gt, lt
  Counter counter_3 (
    .clr(Start_Game_out), .load(comparator_6_eq), .clk(or_7_out), .D(JUMP_ADDR), .Q(ADDR));  // open: up, count, carry
  and and_5 (and_5_out, comparator_3_eq, or_8_out);
  or or_8 (or_8_out, and_8_out, and_7_out);
  and and_6 (and_6_out, and_3_out, s_r_ff_2_q, comparator_5_lt);
  and and_7 (and_7_out, s_r_ff_2_q, ~comparator_5_lt);  // AND_Gate
  Pull_Resistor pull_resistor_2 (.node(controlled_buffer_1_out));
  LED led_1 (.in(controlled_buffer_1_out[0]));
  Button button_1 (.out(Btn_Column[0]));
  LED led_2 (.in(controlled_buffer_2_out[0]));
  LED led_3 (.in(controlled_buffer_2_out[1]));
  LED led_4 (.in(controlled_buffer_2_out[2]));
  LED led_5 (.in(controlled_buffer_2_out[3]));
  LED led_6 (.in(controlled_buffer_2_out[4]));
  LED led_7 (.in(controlled_buffer_2_out[5]));
  LED led_8 (.in(controlled_buffer_2_out[6]));
  LED led_9 (.in(controlled_buffer_2_out[7]));
  LED led_10 (.in(controlled_buffer_2_out[8]));
  LED led_11 (.in(controlled_buffer_2_out[9]));
  LED led_12 (.in(controlled_buffer_2_out[10]));
  LED led_13 (.in(controlled_buffer_2_out[11]));
  LED led_14 (.in(controlled_buffer_2_out[12]));
  LED led_15 (.in(controlled_buffer_2_out[13]));
  LED led_16 (.in(controlled_buffer_2_out[14]));
  LED led_17 (.in(controlled_buffer_2_out[15]));
  // RGB_Video #(.cursor("No Cursor"), .scale(4)) rgb_video_1: pin names not known; wires that end beside it: rgb_video_1_p1, CLK, 1'b1, rgb_video_1_p4[6:0], rgb_video_1_p4[13:7], rgb_video_1_p4[28:14]
  Comparator #(.width(4)) comparator_7 (.a(4'b0001), .b(OPCODE), .eq(rgb_video_1_p1));  // open: gt, lt
  Counter #(.max('hf), .width(4)) counter_4 (
    .clr(or_6_out), .clk(and_5_out), .Q(counter_4_q));  // open: load, up, count, D, carry
  and and_8 (and_8_out, and_11_out, and_12_out);
  ROM #(.addrWidth(6), .dataWidth(3)) UncoveredEmptySquareWith4 (
    .addr(adder_1_out), .data(UncoveredEmptySquareWith4_data));
  ROM #(.addrWidth(6), .dataWidth(3)) UncoveredEmptySquareWith5 (
    .addr(adder_1_out), .data(UncoveredEmptySquareWith5_data));
  ROM #(.addrWidth(6), .dataWidth(3)) UncoveredEmptySquareWith6 (
    .addr(adder_1_out), .data(UncoveredEmptySquareWith6_data));
  ROM #(.addrWidth(6), .dataWidth(3)) UncoveredEmptySquareWith7 (
    .addr(adder_1_out), .data(UncoveredEmptySquareWith7_data));
  ROM #(.addrWidth(6), .dataWidth(3)) UncoveredEmptySquareWith8 (
    .addr(adder_1_out), .data(UncoveredEmptySquareWith8_data));
  LED led_18 (.in(controlled_buffer_1_out[1]));
  LED led_19 (.in(controlled_buffer_1_out[2]));
  LED led_20 (.in(controlled_buffer_1_out[3]));
  Button button_2 (.out(Btn_Column[1]));
  Button button_3 (.out(Btn_Column[2]));
  Button button_4 (.out(Btn_Column[3]));
  Multiplexer #(.select(4), .width(29)) multiplexer_1 (
    .in2(OP2_CANVAS), .in7(OP7_CANVAS), .out(rgb_video_1_p4), .sel(OPCODE));  // open: in0, in1, in3, in4, in5, in6, in8, in9, in10, in11, in12, in13, in14, in15
  Multiplier #(.width(7)) multiplier_1 (.a(counter_1_q), .b(7'b0000100), .out(multiplier_1_out));  // open: cin, cout
  or or_9 (or_9_out, or_6_out, and_12_out);
  Counter #(.max('h7), .trigger("falling"), .width(3)) counter_5 (
    .clr(or_9_out), .clk(and_6_out), .Q(counter_5_q));  // open: load, up, count, D, carry
  assign bit_extender_1_out = {{3{1'b0}}, counter_5_q};  // Bit_Extender bit_extender_1
  LED led_21 (.in(controlled_buffer_1_out[4]));
  LED led_22 (.in(controlled_buffer_1_out[5]));
  Button button_5 (.out(Btn_Column[4]));
  Button button_6 (.out(Btn_Column[5]));
  ROM #(.dataWidth(4)) rom_1 (.addr(ADDR), .data(rom_1_data));
  and and_9 (and_9_out, ~multiplier_1_out[0], ~multiplier_1_out[1], multiplier_1_out[2], multiplier_1_out[3], multiplier_1_out[4], multiplier_1_out[5], multiplier_1_out[6]);  // AND_Gate
  and and_10 (and_10_out, counter_2_q[0], counter_2_q[1], counter_2_q[2], counter_2_q[3]);
  assign bit_extender_2_out = {{3{1'b0}}, counter_2_q};  // Bit_Extender bit_extender_2
  and and_11 (and_11_out, ~counter_8_q[0], counter_8_q[1], counter_8_q[2]);  // AND_Gate
  and and_12 (and_12_out, counter_5_q[0], counter_5_q[1], counter_5_q[2]);
  LED led_23 (.in(controlled_buffer_1_out[6]));
  LED led_24 (.in(controlled_buffer_1_out[7]));
  Button button_7 (.out(Btn_Column[6]));
  Button button_8 (.out(Btn_Column[7]));
  Comparator #(.width(4)) comparator_8 (
    .a(4'b0011), .b(OPCODE), .gt(comparator_8_gt), .eq(comparator_8_eq), .lt(comparator_8_lt));
  or or_10 (or_10_out, comparator_8_lt, comparator_8_gt);
  and and_13 (and_13_out, counter_4_q[0], counter_4_q[1], counter_4_q[2], counter_4_q[3]);
  assign bit_extender_3_out = {{3{1'b0}}, counter_4_q};  // Bit_Extender bit_extender_3
  assign bit_extender_4_out = {{3{1'b0}}, counter_8_q};  // Bit_Extender bit_extender_4
  Multiplier #(.width(6)) multiplier_2 (
    .a(bit_extender_4_out), .b(6'b000111), .out(multiplier_2_out));  // open: cin, cout
  LED led_25 (.in(controlled_buffer_1_out[8]));
  LED led_26 (.in(controlled_buffer_1_out[9]));
  LED led_27 (.in(controlled_buffer_1_out[10]));
  Button button_9 (.out(Btn_Column[8]));
  Button button_10 (.out(Btn_Column[9]));
  Button button_11 (.out(Btn_Column[10]));
  J_K_Flip_Flop #(.trigger("falling")) j_k_ff_1 (
    .J(1'b1), .K(1'b1), .clk(and_14_out), .Q(j_k_ff_1_q), .reset(or_5_out));  // open: Qn, preset
  and and_14 (and_14_out, and_9_out, and_10_out);
  Multiplier #(.width(7)) multiplier_3 (
    .a(7'b0001000), .b(bit_extender_2_out), .out(multiplier_3_out));  // open: cin, cout
  Counter #(.max('h10), .trigger("falling"), .width(5)) counter_6 (
    .clr(or_6_out), .clk(and_13_out), .Q(counter_6_q));  // open: load, up, count, D, carry
  Multiplier #(.width(7)) multiplier_4 (
    .a(bit_extender_3_out), .b(7'b0001000), .out(multiplier_4_out));  // open: cin, cout
  assign bit_extender_5_out = {{4{1'b0}}, counter_5_q};  // Bit_Extender bit_extender_5
  Adder #(.width(6)) adder_1 (.a(multiplier_2_out), .b(bit_extender_1_out), .out(adder_1_out));  // open: cin, cout
  LED led_28 (.in(controlled_buffer_1_out[12]));
  LED led_29 (.in(controlled_buffer_1_out[11]));
  Button button_12 (.out(Btn_Column[12]));
  Button button_13 (.out(Btn_Column[11]));
  and and_15 (and_15_out, ~comparator_10_eq, comparator_8_eq, CLK);  // AND_Gate
  Counter #(.max('h101), .trigger("falling"), .width(9)) counter_7 (
    .clr(or_10_out), .clk(and_15_out), .Q(counter_7_q));  // open: load, up, count, D, carry
  Comparator #(.width(3)) comparator_9 (.a(counter_5_q), .b(3'b111), .eq(comparator_9_eq));  // open: gt, lt
  Adder #(.width(7)) adder_2 (.a(multiplier_4_out), .b(bit_extender_5_out), .out(adder_2_out));  // open: cin, cout
  LED led_30 (.in(controlled_buffer_1_out[13]));
  LED led_31 (.in(controlled_buffer_1_out[14]));
  LED led_32 (.in(controlled_buffer_1_out[15]));
  Button button_14 (.out(Btn_Column[13]));
  Button button_15 (.out(Btn_Column[14]));
  Button button_16 (.out(Btn_Column[15]));
  and and_16 (OP2_FINISH, j_k_ff_1_q, and_14_out);
  assign bit_extender_6_out = {{6{j_k_ff_1_q}}, j_k_ff_1_q};  // Bit_Extender bit_extender_6
  assign not_1_out = ~bit_extender_6_out;  // NOT_Gate not_1, 7 bits wide
  Counter #(.max('h6), .trigger("falling"), .width(3)) counter_8 (
    .clr(or_6_out), .clk(comparator_9_eq), .Q(counter_8_q));  // open: load, up, count, D, carry
  Adder #(.width(7)) adder_3 (.a(adder_2_out), .b(7'b0000001), .out(adder_3_out));  // open: cin, cout
  Button button_17 (.out(Btn_Row[0]));
  Button button_18 (.out(Btn_Row[1]));
  Button button_19 (.out(Btn_Row[2]));
  Button button_20 (.out(Btn_Row[3]));
  Button button_21 (.out(Btn_Row[4]));
  Button button_22 (.out(Btn_Row[5]));
  Button button_23 (.out(Btn_Row[6]));
  Button button_24 (.out(Btn_Row[7]));
  Button button_25 (.out(Btn_Row[8]));
  Button button_26 (.out(Btn_Row[9]));
  Button button_27 (.out(Btn_Row[10]));
  Button button_28 (.out(Btn_Row[11]));
  Button button_29 (.out(Btn_Row[12]));
  Button button_30 (.out(Btn_Row[13]));
  Button button_31 (.out(Btn_Row[14]));
  Button button_32 (.out(Btn_Row[15]));
  D_Flip_Flop #(.trigger("high")) d_ff_1 (.D(rom_1_data[0]), .clk(1'b1), .Q(OPCODE[0]));  // open: Qn, preset, reset
  D_Flip_Flop #(.trigger("high")) d_ff_2 (.D(rom_1_data[1]), .clk(1'b1), .Q(OPCODE[1]));  // open: Qn, preset, reset
  D_Flip_Flop #(.trigger("high")) d_ff_3 (.D(rom_1_data[2]), .clk(1'b1), .Q(OPCODE[2]));  // open: Qn, preset, reset
  D_Flip_Flop #(.trigger("high")) d_ff_4 (.D(rom_1_data[3]), .clk(1'b1), .Q(OPCODE[3]));  // open: Qn, preset, reset
  Bit_Extender #(.in_width(5), .out_width(4)) bit_extender_7 (.in(counter_6_q), .out(bit_extender_7_out));
  Multiplexer #(.select(4), .width(3)) multiplexer_2 (
    .in2(UncoveredMineSquare_data), .in3(SquareWithFlag_data), .in4(UncoveredEmptySquare_data),
    .in5(UncoveredEmptySquareWith1_data), .in6(UncoveredEmptySquareWith2_data),
    .in7(UncoveredEmptySquareWith3_data), .in8(UncoveredEmptySquareWith4_data),
    .in9(UncoveredEmptySquareWith5_data), .in10(UncoveredEmptySquareWith6_data),
    .in11(UncoveredEmptySquareWith7_data), .in12(UncoveredEmptySquareWith8_data), .in13(SquareWithFlag_data),
    .out(multiplexer_2_out), .sel(RAM_OUTPUT));  // open: in0, in1, in14, in15
  assign and_17_out = bit_extender_6_out & multiplier_3_out;  // AND_Gate and_17, 7 bits wide
  assign and_18_out = bit_extender_6_out & multiplier_1_out;  // AND_Gate and_18, 7 bits wide
  assign and_19_out = multiplier_1_out & not_1_out;  // AND_Gate and_19, 7 bits wide
  assign and_20_out = multiplier_3_out & not_1_out;  // AND_Gate and_20, 7 bits wide
  and and_21 (and_21_out, ~counter_6_q[0], ~counter_6_q[1], ~counter_6_q[2], ~counter_6_q[3], counter_6_q[4]);  // AND_Gate
  assign bit_extender_8_out = {{4{1'b0}}, counter_4_q};  // Bit_Extender bit_extender_8
  assign bit_extender_9_out = {{4{1'b0}}, bit_extender_7_out};  // Bit_Extender bit_extender_9
  assign bit_extender_10_out = {{3{1'b0}}, bit_extender_7_out};  // Bit_Extender bit_extender_10
  Button Uncover (.out(Btn_Uncover));
  Button Flag (.out(Btn_Flag));
  Bit_Extender #(.in_width(9), .out_width(8)) bit_extender_11 (.in(counter_7_q), .out(bit_extender_11_out));
  Comparator #(.width(9)) comparator_10 (.a(9'h101), .b(counter_7_q), .eq(comparator_10_eq));  // open: gt, lt
  and and_22 (OP7_FINISH, and_13_out, and_21_out);
  Multiplier multiplier_5 (.a(8'h10), .b(bit_extender_9_out), .out(multiplier_5_out));  // open: cin, cout
  Multiplier #(.width(7)) multiplier_6 (
    .a(bit_extender_10_out), .b(7'b0001000), .out(multiplier_6_out));  // open: cin, cout
  assign bit_extender_12_out = {{4{1'b0}}, counter_8_q};  // Bit_Extender bit_extender_12
  Multiplexer #(.select(3), .width(15)) multiplexer_3 (
    .in0({15{1'b1}}), .in1({15{1'b0}}), .in2(15'h5ddd), .in3(15'h7c00), .out(multiplexer_3_out),
    .sel(multiplexer_2_out));  // open: in4, in5, in6, in7
  assign or_11_out = and_17_out | and_19_out;  // OR_Gate or_11, 7 bits wide
  assign or_12_out = and_18_out | and_20_out;  // OR_Gate or_12, 7 bits wide
  Adder adder_4 (.a(bit_extender_8_out), .b(multiplier_5_out), .out(adder_4_out));  // open: cin, cout
  Adder #(.width(7)) adder_5 (.a(multiplier_6_out), .b(bit_extender_12_out), .out(adder_5_out));  // open: cin, cout
  Adder #(.width(7)) adder_6 (.a(adder_5_out), .b(7'b0000001), .out(adder_6_out));  // open: cin, cout
  and and_23 (OP3_FINISH, comparator_8_eq, comparator_10_eq);
  Canvas_Encoder canvas_encoder_1 (
    .Row(adder_6_out), .Column(adder_3_out), .Color(multiplexer_3_out), .Encode(OP7_CANVAS));
  RAM_Encoder ram_encoder_1 (
    .Address(bit_extender_11_out), .Write_Enable(1'b1), .CLK(and_15_out), .Data(4'b0000), .encode(OP3_RAM));  // open: Address_Disable, Output_Enable, CLK_Default
  Canvas_Encoder canvas_encoder_2 (.Row(or_12_out), .Column(or_11_out), .Color(15'haaa), .Encode(OP2_CANVAS));
  RAM_Encoder ram_encoder_2 (
    .Address(adder_4_out), .Output_Enable(1'b1), .CLK_Default(1'b1), .encode(OP7_RAM));  // open: Address_Disable, Write_Enable, CLK, Data
  or or_13 (or_13_out, OP8_FINISH, OPA_FINISH);
  Comparator #(.width(4)) comparator_11 (
    .a(4'b0100), .b(OPCODE), .gt(comparator_11_gt), .eq(comparator_11_eq), .lt(comparator_11_lt));
  Comparator #(.width(4)) comparator_12 (.a(4'b0101), .b(OPCODE), .eq(comparator_12_eq));  // open: gt, lt
  Comparator #(.width(4)) comparator_13 (.a(4'b0110), .b(OPCODE), .eq(comparator_13_eq));  // open: gt, lt
  assign controlled_buffer_3_out = comparator_13_eq ? Btn_Column : 16'bz;  // Controlled_Buffer controlled_buffer_3
  assign controlled_buffer_4_out = comparator_13_eq ? Btn_Row : 16'bz;  // Controlled_Buffer controlled_buffer_4
  Comparator #(.width(4)) comparator_14 (.a(4'b1000), .b(OPCODE), .eq(comparator_14_eq));  // open: gt, lt
  Multiplexer #(.select(4), .width(17)) multiplexer_4 (
    .in3(OP3_RAM), .in4(OP4_RAM), .in6(OP6_RAM), .in7(OP7_RAM), .in8(OP8_RAM), .in9(OP9_RAM), .in10(OPA_RAM),
    .out(multiplexer_4_out), .sel(OPCODE));  // open: in0, in1, in2, in5, in11, in12, in13, in14, in15
  or or_14 (or_14_out, comparator_11_lt, comparator_11_gt);
  nor nor_1 (nor_1_out, RAM_OUTPUT[0], RAM_OUTPUT[1], RAM_OUTPUT[2], RAM_OUTPUT[3]);
  T_Flip_Flop #(.trigger("falling")) t_ff_1 (
    .T(1'b1), .clk(and_24_out), .Q(t_ff_1_q), .reset(OP5_FINISH));  // open: Qn, preset
  and and_24 (and_24_out, comparator_12_eq, CLK);
  and and_25 (and_25_out, comparator_14_eq, CLK);
  Pull_Resistor pull_resistor_3 (.node(pull_resistor_3_node));
  assign pull_resistor_3_node = OP6_FINISH ? OP6_JUMP_ADDR : 8'bz;  // Controlled_Buffer controlled_buffer_5
  Pull_Resistor pull_resistor_4 (.node(pull_resistor_4_node));
  assign pull_resistor_4_node = or_13_out ? 8'h4 : 8'bz;  // Controlled_Buffer controlled_buffer_6
  Pull_Resistor pull_resistor_5 (.node(pull_resistor_5_node));
  assign pull_resistor_5_node = OP9_FINISH ? {8{1'b1}} : 8'bz;  // Controlled_Buffer controlled_buffer_7
  Counter #(.max('h28), .width(6)) counter_9 (
    .clr(or_14_out), .clk(nor_1_out), .Q(counter_9_q));  // open: load, up, count, D, carry
  and and_26 (and_26_out, comparator_13_eq, Btn_Uncover);
  and and_27 (and_27_out, comparator_13_eq, Btn_Flag);
  not not_2 (not_2_out, multiplexer_4_out[0]);
  and and_28 (and_28_out, multiplexer_4_out[11], ~multiplexer_4_out[16]);  // AND_Gate
  and and_29 (and_29_out, multiplexer_4_out[16], CLK);
  T_Flip_Flop #(.trigger("falling")) t_ff_2 (
    .T(1'b1), .clk(t_ff_1_q), .Q(t_ff_2_q), .reset(OP5_FINISH));  // open: Qn, preset
  not not_3 (not_3_out, comparator_14_eq);
  Comparator #(.width(4)) comparator_15 (.a(RAM_OUTPUT), .b(4'b0001), .eq(comparator_15_eq));  // open: gt, lt
  Comparator #(.width(4)) comparator_16 (.a(RAM_OUTPUT), .b(4'b1101), .eq(comparator_16_eq));  // open: gt, lt
  or or_15 (or_15_out, and_28_out, and_29_out);
  and and_30 (and_30_out, CLK, comparator_11_eq, ~comparator_24_eq);  // AND_Gate
  and and_31 (OP5_FINISH, t_ff_1_q, t_ff_2_q);
  Encoder_4bit encoder_4bit_1 (.I(controlled_buffer_3_out), .O(encoder_4bit_1_o));
  D_Flip_Flop d_ff_5 (.D(encoder_4bit_1_o[3]), .clk(or_gate_16bit_1_q), .Q(OP6_Column[3]));  // open: Qn, preset, reset
  OR_Gate_16bit or_gate_16bit_1 (.I(controlled_buffer_3_out), .Q(or_gate_16bit_1_q));  // open: not_Q
  Encoder_4bit encoder_4bit_2 (.I(controlled_buffer_4_out), .O(encoder_4bit_2_o));
  D_Flip_Flop d_ff_6 (.D(encoder_4bit_2_o[3]), .clk(or_gate_16bit_2_q), .Q(OP6_Row[3]));  // open: Qn, preset, reset
  OR_Gate_16bit or_gate_16bit_2 (.I(controlled_buffer_4_out), .Q(or_gate_16bit_2_q));  // open: not_Q
  Comparator #(.mode("unsigned"), .width(4)) comparator_17 (
    .a(RAM_OUTPUT), .b(4'b0000), .eq(comparator_17_eq));  // open: gt, lt
  Comparator #(.mode("unsigned"), .width(4)) comparator_18 (
    .a(RAM_OUTPUT), .b(4'b0001), .eq(comparator_18_eq));  // open: gt, lt
  Comparator #(.mode("unsigned"), .width(4)) comparator_19 (
    .a(RAM_OUTPUT), .b(4'b0000), .eq(comparator_19_eq));  // open: gt, lt
  Comparator #(.mode("unsigned"), .width(4)) comparator_20 (
    .a(RAM_OUTPUT), .b(4'b0001), .eq(comparator_20_eq));  // open: gt, lt
  Comparator #(.mode("unsigned"), .width(4)) comparator_21 (
    .a(RAM_OUTPUT), .b(4'b0011), .eq(comparator_21_eq));  // open: gt, lt
  Comparator #(.mode("unsigned"), .width(4)) comparator_22 (
    .a(RAM_OUTPUT), .b(4'b1101), .eq(comparator_22_eq));  // open: gt, lt
  Register register_1 (.D(RAM_ADDR), .en(comparator_14_eq), .clk(comparator_14_eq), .Q(register_1_q));  // open: clr
  Comparator #(.mode("unsigned"), .width(2)) comparator_23 (
    .a(counter_10_q), .b(2'b01), .gt(comparator_23_gt));  // open: eq, lt
  or or_16 (or_16_out, comparator_15_eq, comparator_16_eq);
  or or_17 (or_17_out, OP6_FINISH, or_13_out, OP9_FINISH, 1'b0);
  assign or_18_out = pull_resistor_3_node | pull_resistor_4_node | pull_resistor_5_node | {8{1'b0}};  // OR_Gate or_18, 8 bits wide
  Register register_2 (.D(multiplexer_4_out[8:1]), .en(not_2_out), .clk(or_15_out), .Q(RAM_ADDR));  // open: clr
  Random random_1 (.clr(and_30_out), .out(random_1_out));  // open: next, clk
  Comparator #(.width(6)) comparator_24 (.a(6'b101000), .b(counter_9_q), .eq(comparator_24_eq));  // open: gt, lt
  D_Flip_Flop d_ff_7 (.D(encoder_4bit_1_o[2]), .clk(or_gate_16bit_1_q), .Q(OP6_Column[2]));  // open: Qn, preset, reset
  D_Flip_Flop d_ff_8 (.D(encoder_4bit_2_o[2]), .clk(or_gate_16bit_2_q), .Q(OP6_Row[2]));  // open: Qn, preset, reset
  and and_32 (and_32_out, and_26_out, comparator_17_eq);
  and and_33 (and_33_out, and_26_out, comparator_18_eq);
  and and_34 (and_34_out, and_27_out, comparator_19_eq);
  and and_35 (and_35_out, and_27_out, comparator_20_eq);
  and and_36 (and_36_out, and_27_out, comparator_21_eq);
  and and_37 (and_37_out, and_27_out, comparator_22_eq);
  Counter #(.max('h3), .width(2)) counter_10 (
    .clr(or_19_out), .clk(and_25_out), .Q(counter_10_q));  // open: load, up, count, D, carry
  or or_19 (or_19_out, and_40_out, not_3_out);
  Register #(.trigger("high")) register_3 (.D(or_18_out), .en(1'b1), .clk(or_17_out), .Q(register_3_q));  // open: clr
  Comparator #(.mode("unsigned")) comparator_25 (.a(register_1_q), .b(8'hf), .gt(comparator_25_gt));  // open: eq, lt
  Comparator #(.mode("unsigned")) comparator_26 (.a(register_1_q), .b(8'hf0), .lt(comparator_26_lt));  // open: gt, eq
  BitSelector #(.group(4)) bitselector_1 (.in(register_1_q), .out(bitselector_1_out), .sel(1'b0));
  Comparator #(.mode("unsigned"), .width(4)) comparator_27 (
    .a(bitselector_1_out), .b(4'b0000), .gt(comparator_27_gt), .lt(comparator_27_lt));  // open: eq
  BitSelector #(.group(4)) bitselector_2 (.in(register_1_q), .out(bitselector_2_out), .sel(1'b0));
  Comparator #(.mode("unsigned"), .width(4)) comparator_28 (
    .a(bitselector_2_out), .b(4'b1111), .gt(comparator_28_gt), .lt(comparator_28_lt));  // open: eq
  Counter #(.max('h18), .width(5)) counter_11 (
    .clr(not_4_out), .clk(and_38_out), .Q(counter_11_q));  // open: load, up, count, D, carry
  not not_4 (not_4_out, comparator_14_eq);
  and and_38 (and_38_out, and_25_out, comparator_32_lt, comparator_23_gt, or_16_out);
  RAM #(.dataWidth(4), .\type ("nonvolatile")) ram_1 (
    .addr(RAM_ADDR), .we(multiplexer_4_out[9]), .oe(multiplexer_4_out[10]), .clk(or_15_out),
    .din(multiplexer_4_out[15:12]), .dout(RAM_OUTPUT));
  and and_39 (OP4_FINISH, comparator_11_eq, comparator_24_eq);
  D_Flip_Flop d_ff_9 (.D(encoder_4bit_1_o[1]), .clk(or_gate_16bit_1_q), .Q(OP6_Column[1]));  // open: Qn, preset, reset
  D_Flip_Flop d_ff_10 (.D(encoder_4bit_2_o[1]), .clk(or_gate_16bit_2_q), .Q(OP6_Row[1]));  // open: Qn, preset, reset
  or or_20 (or_20_out, and_34_out, and_35_out, and_36_out, and_37_out);
  or or_21 (or_21_out, comparator_27_gt, comparator_27_lt);
  or or_22 (or_22_out, comparator_28_gt, comparator_28_lt);
  Comparator #(.mode("unsigned")) comparator_29 (
    .a(register_3_q), .b({8{1'b0}}), .gt(comparator_29_gt), .eq(comparator_29_eq));  // open: lt
  D_Flip_Flop d_ff_11 (.D(encoder_4bit_1_o[0]), .clk(or_gate_16bit_1_q), .Q(OP6_Column[0]));  // open: Qn, preset, reset
  D_Flip_Flop d_ff_12 (.D(encoder_4bit_2_o[0]), .clk(or_gate_16bit_2_q), .Q(OP6_Row[0]));  // open: Qn, preset, reset
  assign bit_extender_13_out = {{7{and_32_out}}, and_32_out};  // Bit_Extender bit_extender_13
  assign bit_extender_14_out = {{7{and_33_out}}, and_33_out};  // Bit_Extender bit_extender_14
  assign bit_extender_15_out = {{7{or_20_out}}, or_20_out};  // Bit_Extender bit_extender_15
  and and_40 (and_40_out, counter_10_q[0], counter_10_q[1]);
  assign controlled_buffer_8_out = comparator_25_gt ? register_1_q : 8'bz;  // Controlled_Buffer controlled_buffer_8
  assign controlled_buffer_9_out = comparator_26_lt ? register_1_q : 8'bz;  // Controlled_Buffer controlled_buffer_9
  assign controlled_buffer_10_out = or_21_out ? register_1_q : 8'bz;  // Controlled_Buffer controlled_buffer_10
  assign controlled_buffer_11_out = or_22_out ? register_1_q : 8'bz;  // Controlled_Buffer controlled_buffer_11
  Pull_Resistor pull_resistor_6 (.node(pull_resistor_6_node));
  assign pull_resistor_6_node = comparator_29_gt ? register_3_q : 8'bz;  // Controlled_Buffer controlled_buffer_12
  Pull_Resistor pull_resistor_7 (.node(pull_resistor_7_node));
  assign pull_resistor_7_node = comparator_29_eq ? 8'h4 : 8'bz;  // Controlled_Buffer controlled_buffer_13
  assign bit_extender_16_out = {{4{1'b0}}, OP6_Column};  // Bit_Extender bit_extender_16
  assign bit_extender_17_out = {{4{1'b0}}, OP6_Row};  // Bit_Extender bit_extender_17
  assign and_41_out = bit_extender_13_out & 8'h6;  // AND_Gate and_41, 8 bits wide
  assign and_42_out = bit_extender_14_out & 8'hb;  // AND_Gate and_42, 8 bits wide
  assign and_43_out = bit_extender_15_out & 8'h10;  // AND_Gate and_43, 8 bits wide
  Subtractor subtractor_1 (.a(controlled_buffer_8_out), .b(8'h10), .out(subtractor_1_out));  // open: bin, bout
  Adder adder_7 (.a(controlled_buffer_9_out), .b(8'h10), .out(adder_7_out));  // open: cin, cout
  Subtractor subtractor_2 (.a(controlled_buffer_10_out), .b(8'h1), .out(subtractor_2_out));  // open: bin, bout
  Adder adder_8 (.a(controlled_buffer_11_out), .b(8'h1), .out(adder_8_out));  // open: cin, cout
  assign JUMP_ADDR = pull_resistor_6_node | pull_resistor_7_node;  // OR_Gate or_23, 8 bits wide
  RAM_Encoder ram_encoder_3 (
    .Address(random_1_out), .Write_Enable(nor_1_out), .Output_Enable(1'b1), .CLK(and_30_out), .Data(4'b0001),
    .encode(OP4_RAM));  // open: Address_Disable, CLK_Default
  Multiplier multiplier_7 (.a(8'h10), .b(bit_extender_17_out), .out(multiplier_7_out));  // open: cin, cout
  assign OP6_JUMP_ADDR = and_41_out | and_42_out | and_43_out;  // OR_Gate or_24, 8 bits wide
  and and_44 (and_44_out, and_40_out, and_25_out);
  Adder #(.width(5)) adder_9 (.a(5'b00001), .b(counter_11_q), .out(adder_9_out));  // open: cin, cout
  Adder adder_10 (.a(bit_extender_16_out), .b(multiplier_7_out), .out(adder_10_out));  // open: cin, cout
  Counter #(.max('ha), .width(4)) counter_12 (
    .clr(not_3_out), .clk(and_44_out), .Q(counter_12_q));  // open: load, up, count, D, carry
  and and_45 (and_45_out, comparator_25_gt, or_21_out);
  and and_46 (and_46_out, comparator_25_gt, or_22_out);
  and and_47 (and_47_out, comparator_26_lt, or_21_out);
  and and_48 (and_48_out, comparator_26_lt, or_22_out);
  Divider #(.width(5)) divider_1 (.a(adder_9_out), .b(5'b00011), .out(divider_1_out));  // open: upper, rem
  or or_25 (OP6_FINISH, and_32_out, and_33_out, or_20_out);
  assign controlled_buffer_14_out = and_45_out ? register_1_q : 8'bz;  // Controlled_Buffer controlled_buffer_14
  assign controlled_buffer_15_out = and_46_out ? register_1_q : 8'bz;  // Controlled_Buffer controlled_buffer_15
  assign controlled_buffer_16_out = and_47_out ? register_1_q : 8'bz;  // Controlled_Buffer controlled_buffer_16
  assign controlled_buffer_17_out = and_48_out ? register_1_q : 8'bz;  // Controlled_Buffer controlled_buffer_17
  Bit_Extender #(.in_width(5), .out_width(4)) bit_extender_18 (.in(divider_1_out), .out(bit_extender_18_out));
  Subtractor subtractor_3 (.a(controlled_buffer_14_out), .b(8'h11), .out(subtractor_3_out));  // open: bin, bout
  Subtractor subtractor_4 (.a(controlled_buffer_15_out), .b(8'hf), .out(subtractor_4_out));  // open: bin, bout
  Adder adder_11 (.a(controlled_buffer_16_out), .b(8'hf), .out(adder_11_out));  // open: cin, cout
  Adder adder_12 (.a(controlled_buffer_17_out), .b(8'h11), .out(adder_12_out));  // open: cin, cout
  Adder #(.width(4)) adder_13 (.a(4'b0100), .b(bit_extender_18_out), .out(adder_13_out));  // open: cin, cout
  RAM_Encoder ram_encoder_4 (
    .Address(adder_10_out), .Output_Enable(1'b1), .CLK_Default(1'b1), .encode(OP6_RAM));  // open: Address_Disable, Write_Enable, CLK, Data
  Multiplexer #(.select(4), .width(8)) multiplexer_5 (
    .in0(subtractor_1_out), .in1(adder_7_out), .in2(subtractor_2_out), .in3(adder_8_out),
    .in4(subtractor_3_out), .in5(subtractor_4_out), .in6(adder_11_out), .in7(adder_12_out),
    .in8(register_1_q), .out(multiplexer_5_out), .sel(counter_12_q));  // open: in9, in10, in11, in12, in13, in14, in15
  Comparator #(.mode("unsigned"), .width(4)) comparator_30 (
    .a(counter_12_q), .b(4'b1010), .eq(OP8_FINISH));  // open: gt, lt
  Comparator #(.mode("unsigned"), .width(4)) comparator_31 (
    .a(counter_12_q), .b(4'b1001), .eq(comparator_31_eq));  // open: gt, lt
  Comparator #(.mode("unsigned"), .width(4)) comparator_32 (
    .a(counter_12_q), .b(4'b1000), .eq(comparator_32_eq), .lt(comparator_32_lt));  // open: gt
  Comparator #(.width(4)) comparator_33 (
    .a(4'b1001), .b(OPCODE), .gt(comparator_33_gt), .eq(comparator_33_eq), .lt(comparator_33_lt));
  Comparator #(.width(4)) comparator_34 (.a(4'b1010), .b(OPCODE), .eq(comparator_34_eq));  // open: gt, lt
  and and_49 (and_49_out, CLK, comparator_33_eq);
  or or_26 (or_26_out, comparator_33_gt, comparator_33_lt);
  and and_50 (OPA_FINISH, comparator_34_eq, CLK);
  Comparator #(.mode("unsigned"), .width(4)) comparator_35 (
    .a(RAM_OUTPUT), .b(4'b0000), .eq(comparator_35_eq));  // open: gt, lt
  assign controlled_buffer_18_out = comparator_35_eq ? 4'b0011 : 4'bz;  // Controlled_Buffer controlled_buffer_18
  Comparator #(.mode("unsigned"), .width(4)) comparator_36 (
    .a(RAM_OUTPUT), .b(4'b0001), .eq(comparator_36_eq));  // open: gt, lt
  assign controlled_buffer_19_out = comparator_36_eq ? 4'b1101 : 4'bz;  // Controlled_Buffer controlled_buffer_19
  Comparator #(.mode("unsigned"), .width(4)) comparator_37 (
    .a(RAM_OUTPUT), .b(4'b0011), .eq(comparator_37_eq));  // open: gt, lt
  assign controlled_buffer_20_out = comparator_37_eq ? 4'b0000 : 4'bz;  // Controlled_Buffer controlled_buffer_20
  Comparator #(.mode("unsigned"), .width(4)) comparator_38 (
    .a(RAM_OUTPUT), .b(4'b1101), .eq(comparator_38_eq));  // open: gt, lt
  assign controlled_buffer_21_out = comparator_38_eq ? 4'b0001 : 4'bz;  // Controlled_Buffer controlled_buffer_21
  and and_51 (and_51_out, ~and_40_out, comparator_31_eq);  // AND_Gate
  and and_52 (and_52_out, ~and_40_out, comparator_32_eq);  // AND_Gate
  T_Flip_Flop #(.trigger("falling")) t_ff_3 (
    .T(1'b1), .clk(and_49_out), .Q(t_ff_3_q), .reset(or_26_out));  // open: Qn, preset
  Pull_Resistor pull_resistor_8 (.node(controlled_buffer_18_out));
  Pull_Resistor pull_resistor_9 (.node(controlled_buffer_19_out));
  Pull_Resistor pull_resistor_10 (.node(controlled_buffer_20_out));
  Pull_Resistor pull_resistor_11 (.node(controlled_buffer_21_out));
  not not_5 (not_5_out, and_52_out);
  assign controlled_buffer_22_out = not_5_out ? ram_encoder_5_encode : 17'bz;  // Controlled_Buffer controlled_buffer_22
  RAM_Encoder ram_encoder_5 (
    .Address(multiplexer_5_out), .Output_Enable(1'b1), .CLK_Default(1'b1), .encode(ram_encoder_5_encode));  // open: Address_Disable, Write_Enable, CLK, Data
  assign controlled_buffer_23_out = and_51_out ? ram_encoder_6_encode : 17'bz;  // Controlled_Buffer controlled_buffer_23
  RAM_Encoder ram_encoder_6 (
    .Address(register_1_q), .Write_Enable(1'b1), .Data(adder_13_out), .CLK_Default(1'b1),
    .encode(ram_encoder_6_encode));  // open: Address_Disable, Output_Enable, CLK
  Counter counter_13 (.clr(or_26_out), .clk(t_ff_3_q), .Q(counter_13_q));  // open: load, up, count, D, carry
  Pull_Resistor pull_resistor_12 (.node(controlled_buffer_22_out));
  Pull_Resistor pull_resistor_13 (.node(controlled_buffer_23_out));
  assign or_27_out = controlled_buffer_18_out | controlled_buffer_19_out | controlled_buffer_20_out | controlled_buffer_21_out;  // OR_Gate or_27, 4 bits wide
  assign OP8_RAM = controlled_buffer_22_out | controlled_buffer_23_out;  // OR_Gate or_28, 17 bits wide
  Comparator #(.width(4)) comparator_39 (.a(RAM_OUTPUT), .b(4'b0001), .eq(comparator_39_eq));  // open: gt, lt
  Comparator #(.width(4)) comparator_40 (.a(RAM_OUTPUT), .b(4'b1101), .eq(comparator_40_eq));  // open: gt, lt
  or or_29 (or_29_out, comparator_39_eq, comparator_40_eq);
  RAM_Encoder ram_encoder_7 (
    .Address_Disable(1'b1), .Write_Enable(1'b1), .CLK(OPA_FINISH), .Data(or_27_out), .encode(OPA_RAM));  // open: Address, Output_Enable, CLK_Default
  Comparator comparator_41 (.a({8{1'b0}}), .b(counter_13_q), .eq(comparator_41_eq));  // open: gt, lt
  D_Flip_Flop #(.trigger("falling")) d_ff_13 (
    .D(1'b1), .clk(and_53_out), .Q(d_ff_13_q), .reset(or_26_out));  // open: Qn, preset
  and and_53 (and_53_out, t_ff_3_q, comparator_41_eq);
  and and_54 (OP9_FINISH, d_ff_13_q, and_53_out);
  RAM_Encoder ram_encoder_8 (
    .Address(counter_13_q), .Write_Enable(or_29_out), .Output_Enable(1'b1), .CLK(and_49_out), .Data(4'b0010),
    .encode(OP9_RAM));  // open: Address_Disable, CLK_Default

  // Other names for the same wires on the sheet: OP1_FINISH = CLS

  // Notes on the sheet:
  //   Clear Screen (OPCODE: 1)
  //   Draw Grid (OPCODE: 2)
  //   Render Screen (OPCODE: 7)
  //   contents of UncoveredMineSquare (hex, n*v repeats v):
  //   9*0 1 1 1 0 0 0 1 2 1 1 1 0 0 5*1 0 0 5*1 0 0 0 1 1 1
  //   contents of SquareWithFlag (hex, n*v repeats v):
  //   10*1 3 3 0 1 1 4*3 0 1 1 3 3 3 1 0 6*1 0 6*1 0 8*1
  //   contents of UncoveredEmptySquareWith1 (hex, n*v repeats v):
  //   9*0 1 1 6*0 1 6*0 1 6*0 1 5*0 1 1 1
  //   contents of UncoveredEmptySquareWith2 (hex, n*v repeats v):
  //   9*0 1 1 1 6*0 1 4*0 1 1 1 4*0 1 6*0 1 1 1
  //   contents of UncoveredEmptySquareWith3 (hex, n*v repeats v):
  //   9*0 1 1 1 6*0 1 4*0 1 1 1 6*0 1 4*0 1 1 1
  //   contents of UncoveredEmptySquareWith4 (hex, n*v repeats v):
  //   9*0 1 0 1 4*0 1 0 1 4*0 1 1 1 6*0 1 6*0 1
  //   contents of UncoveredEmptySquareWith5 (hex, n*v repeats v):
  //   9*0 1 1 1 4*0 1 6*0 1 1 1 6*0 1 4*0 1 1 1
  //   contents of UncoveredEmptySquareWith6 (hex, n*v repeats v):
  //   9*0 1 1 1 4*0 1 6*0 1 1 1 4*0 1 0 1 4*0 1 1 1
  //   contents of UncoveredEmptySquareWith7 (hex, n*v repeats v):
  //   9*0 1 1 1 4*0 1 0 1 6*0 1 6*0 1 6*0 1
  //   contents of UncoveredEmptySquareWith8 (hex, n*v repeats v):
  //   9*0 1 1 1 4*0 1 0 1 4*0 1 1 1 4*0 1 0 1 4*0 1 1 1
  //   Reset RAM (OPCODE: 3)
  //   contents of rom_1 (hex, n*v repeats v):
  //   1 3 4 2 6 5 8 1 2 7 5 9 1 2 7 5 a 1 2 7 5
  //   Jump Dest. Address Register
  //   RAM for Game Data
  //   Set Mines (OPCODE: 4)
  //   Jump (OPCODE: 5)
  //   Standby for Selection (OPCODE: 6)
  //   Uncover (OPCODE: 8)
  //   Game Over (OPCODE: 9)
  //   Flagging (OPCODE: A)
endmodule

module OR_Gate_16bit (
  input  [15:0] I,
  output Q,
  output not_Q
);

  or or_1 (Q, I[0], I[1], I[2], I[3], I[4], I[5], I[6], I[7], I[8], I[9], I[10], I[11], I[12], I[13], I[14], I[15]);
  not not_1 (not_Q, Q);
endmodule

module Encoder_4bit (
  input  [15:0] I,
  output [3:0] O
);

  PLA #(.in_width(16), .out_width(4), .\table ("0000000000000001 0000\n0000000000000010 0001\n0000000000000100 0010\n0000000000001000 0011\n0000000000010000 0100\n0000000000100000 0101\n0000000001000000 0110\n0000000010000000 0111\n0000000100000000 1000\n0000001000000000 1001\n0000010000000000 1010\n0000100000000000 1011\n0001000000000000 1100\n0010000000000000 1101\n0100000000000000 1110\n1000000000000000 1111")) Encoder_4bit (
    .in(I), .out(O));
endmodule

module Decoder_4bit (
  input  [3:0] I,
  output [15:0] O
);

  PLA #(.in_width(4), .out_width(16), .\table ("0000 0000000000000001\n0001 0000000000000010\n0010 0000000000000100\n0011 0000000000001000\n0100 0000000000010000\n0101 0000000000100000\n0110 0000000001000000\n0111 0000000010000000\n1000 0000000100000000\n1001 0000001000000000\n1010 0000010000000000\n1011 0000100000000000\n1100 0001000000000000\n1101 0010000000000000\n1110 0100000000000000\n1111 1000000000000000")) Decoder_4bit (
    .in(I), .out(O));
endmodule

module Canvas_Encoder (
  input  [6:0] Row,
  input  [6:0] Column,
  input  [14:0] Color,
  output [28:0] Encode
);


  assign Encode = {Color, Row, Column};
endmodule

module RAM_Encoder (
  input  Address_Disable,
  input  [7:0] Address,
  input  Write_Enable,
  input  Output_Enable,
  input  CLK,
  input  [3:0] Data,
  input  CLK_Default,
  output [16:0] encode
);

  Pull_Resistor pull_resistor_1 (.node(Address_Disable));
  Pull_Resistor pull_resistor_2 (.node(CLK_Default));

  assign encode = {CLK_Default, Data, CLK, Output_Enable, Write_Enable, Address, Address_Disable};
endmodule
